# Fritzing sketch scheme (saved by Fritzing 0.7.11b)
breadboards: 1

parts:
  U1 = Arduino Mega
  R1 = Resistor [tolerance=±5% resistance=10k package=THT]
  R2 = Resistor [tolerance=±5% resistance=10k package=THT]
  S1 = Reed switch [package=THT]
  S2 = Reed switch [package=THT]
  U5 = mystery part, 3 pins [chip_label=DS18B20 spacing=300mil]
  Nokia_5110_LCD_Module2 = Nokia5110LCDModule
  R3 = Resistor [tolerance=±5% resistance=10k package=THT]
  S3 = Pushbutton [package="[THT]"]
  R4 = Resistor [tolerance=±5% resistance=10k package=THT]

nets:
  N1: U1.GND, U1.D8, R1.Pin_1, R2.Pin_1, U5.pin1, U5.pin3, Nokia_5110_LCD_Module2.SCLK, R3.Pin_0, S3.Pin_3, S3.Pin_4, R4.Pin_0
  N2: U1.D7, Nokia_5110_LCD_Module2.Grnd
  N3: U1.D6, Nokia_5110_LCD_Module2.Vcc
  N4: U1.D5, Nokia_5110_LCD_Module2.SCE
  N5: U1.D4, Nokia_5110_LCD_Module2.RST
  N6: U1.D3, Nokia_5110_LCD_Module2.D/C
  N7: U1.D2, U5.pin2, R3.Pin_1
  N8: U1.3V3, S1.pin_1, S2.pin_1, Nokia_5110_LCD_Module2.6_DN_(MOSI)
  N9: U1.A0, R1.Pin_0, S2.pin_2
  N10: U1.A1, R2.Pin_0, S1.pin_2
  N11: S3.Pin_1, S3.Pin_2, R4.Pin_1

custom parts:
  : Nokia 5110 LCD with 8 pin. It's a 45mm*45mm module part. Description: The Nokia 5110 is a basic graphic LCD screen for lots of applications. It was originally intended for as a cell phone screen. This one is mounted on an easy to solder PCB. It uses the PCD8544 controller. The PCD8544 is a low power CMOS LCD controller/driver, designed to drive a graphic display of 48 rows and 84 columns. All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
