# Fritzing sketch scheme2 (saved by Fritzing 0.7.11b)
breadboards: 1

parts:
  U1 = Arduino Mega
  R1 = Resistor [tolerance=±5% resistance=10k package=THT]
  R2 = Resistor [tolerance=±5% resistance=10k package=THT]
  S1 = Reed switch [package=THT]
  S2 = Reed switch [package=THT]
  U5 = mystery part, 3 pins [chip_label=DS18B20 spacing=300mil]
  R3 = Resistor [tolerance=±5% resistance=4.7k package=THT]
  R4 = Resistor [tolerance=±5% resistance=10k package=THT]
  S3 = Pushbutton [package="[THT]"]
  C1 = Electrolytic Capacitor [capacitance=10µF package="100 mil [THT, electrolytic]"]  # not connected

nets (from the breadboard view):
  N1: U1.D8, R4.Pin_0, S3.Pin_1, S3.Pin_2
  N2: U1.3V3, S1.pin_1, S2.pin_1, U5.pin2, U5.pin3, R3.Pin_0, R3.Pin_1, S3.Pin_3, S3.Pin_4
  N3: U1.GND, R1.Pin_1, R2.Pin_1, U5.pin1
  N4: U1.A0, R1.Pin_0, S2.pin_2
  N5: U1.A1, R2.Pin_0, S1.pin_2
